# Fritzing sketch geiger-wifi (saved by Fritzing 0.9.3b)

parts:
  WeMos_D1_Mini1 = WeMos D1 Mini
  OLED_I2C1 = OLED 128x64 I2C Monochrome Display
  JP1 = FTDI_BASIC [package=ftdi_basic]  # not connected

nets:
  3V3: WeMos_D1_Mini1.3V3, OLED_I2C1.VDD
  N1: WeMos_D1_Mini1.D1, OLED_I2C1.SDA
  N2: WeMos_D1_Mini1.D2, OLED_I2C1.SCK
  N3: WeMos_D1_Mini1.G, OLED_I2C1.GND

notes:
  Serial Connector of the MightyOhm Geiger Counter

custom parts:
  WeMos D1 Mini: The D1 mini is a mini wifi board based on ESP-8266EX.
